# Fritzing sketch knocker (saved by Fritzing 0.9.3b)

parts:
  부품1 = Arduino Uno (Rev3) - ICSP
  BT1 = Bluetooth HC-06u [package=THT]
  LED1 = smd LED [color="Red (633nm)" package="0603 [SMD]"]
  LED2 = smd LED [color="Green (555nm)" package="0603 [SMD]"]
  S1 = Pushbutton [package="[SMD]"]
  R1 = Resistor [tolerance=±5% resistance=11 package="1206 [SMD]"]
  R2 = Resistor [tolerance=±5% resistance=11 package="1206 [SMD]"]
  R3 = Resistor [tolerance=±5% resistance=11 package="1206 [SMD]"]
  J1 = Piezo Speaker

nets:
  N1: 부품1.D8, J1.pin2
  N2: 부품1.D10_PWM/SS, R1.Pin_1
  N3: 부품1.D11_PWM/MOSI, R2.Pin_1
  GND: 부품1.GND, BT1.GND, LED1.cathode, LED2.cathode, R3.Pin_0
  N4: 부품1.D2, BT1.TXD
  N5: 부품1.D3_PWM, BT1.RXD
  N6: 부품1.D6_PWM, S1.Pin_3, S1.Pin_4, R3.Pin_1
  3V3: 부품1.3V3, BT1.VCC
  N7: 부품1.5V, S1.Pin_1, S1.Pin_2
  N8: LED1.anode, R1.Pin_0
  N9: LED2.anode, R2.Pin_0

custom parts:
  Bluetooth HC-06u: Bluetooth HC-06 - face up, pins down 16.5mm x 37.5mm PCB
